# Fritzing sketch Sketch (saved by Fritzing 0.9.3b)

parts:
  Raspberry_Pi_1 = Raspberry Pi 3 [part_number=RPI-3-V1.2]
  L298N1 = L298N DC motor driver
  BAT1 = BC9VPC [package=bc9vpc]

nets:
  N1: Raspberry_Pi_1.GIPO19, L298N1.ENB
  N2: Raspberry_Pi_1.GIPO20, L298N1.IN3
  N3: Raspberry_Pi_1.GIPO16, L298N1.IN4
  N4: Raspberry_Pi_1.GIPO18, L298N1.ENA
  N5: Raspberry_Pi_1.GIPO15, L298N1.IN1
  N6: Raspberry_Pi_1.GIPO14, L298N1.IN2
  GND: Raspberry_Pi_1.GND, L298N1.GND
  N7: L298N1.12V, BAT1.V+

notes:
  C1
  C2
  9V
  GND
  Servo Motor
  XL Motor

custom parts:
  L298N DC motor driver: 2x DC motor driver with 78M05 positive voltage regulator (7..35 V) L298N: max 46 V, 2 A Set 5 V Enable jumper to enable 5 V regultor (needed for the L298N) and +5 V output at screw terminal or supply external +5 V at screw terminal Set ENA and/or ENB to +5 V to enable motor permanently or supply ENA and/or ENB with PWM signal IN1 and IN2 set rotation directory for motor A (OUT1/OUT2) IN2 and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
